// Logisim project s-mips.circ as structural Verilog: 13 circuits, main circuit S-MIPS Board
module S_MIPS_Board (
  input  DESHABILITAR_DISPATCHER,
  output halt
);

  wire button_1_out, CLK, CS, d_ff_1_q, LCLR, LoadRAM, LoadRAMOn, LW, R_R_W, R_W, ram_dispatcher_1_finished,
       RCS, Reset_out, RST, TTY_EN;
  wire [2:0] KDB;
  wire [3:0] LMask, Mask, ram_1_read_time, ram_1_write_time, RMask;
  wire [6:0] KDB_DATA, TTY_DATA;
  wire [15:0] Addr, LAddr, RAddr;
  wire [31:0] I0, I1, I2, I3, LData, ram_1_data_out_0, ram_1_data_out_1, ram_1_data_out_2, ram_1_data_out_3,
       RI0, RI1, RI2, RI3;

  TTY #(.rows(25), .cols(80)) tty_1 (.data(TTY_DATA), .clk(CLK), .we(TTY_EN), .clr(RST));
  not not_1 (LoadRAMOn, ram_dispatcher_1_finished);
  RAM_Dispatcher ram_dispatcher_1 (
    .WriteTime(ram_1_write_time), .Clock(CLK), .Data(LData), .Address(LAddr), .Mask(LMask),
    .Finished(ram_dispatcher_1_finished), .Write(LW), .CLR(LCLR));
  Keyboard #(.buflen(64)) keyboard_1 (.clk(CLK), .re(KDB[0]), .avail(KDB[2]), .data(KDB_DATA));  // open: clr
  RAM ram_1 (
    .Address(RAddr), .Data_Out_0(ram_1_data_out_0), .Data_Out_1(ram_1_data_out_1),
    .Data_Out_2(ram_1_data_out_2), .Data_Out_3(ram_1_data_out_3), .Data_In_0(RI0), .Data_In_1(RI1),
    .Data_In_2(RI2), .Data_In_3(RI3), .Mask(RMask), .nRead_Write(R_R_W), .Chip_Select(RCS),
    .Read_Time(ram_1_read_time), .Reset(button_1_out), .Write_Time(ram_1_write_time));
  Button button_1 (.out(button_1_out));
  D_Flip_Flop d_ff_1 (.clk(CLK), .D(1'b1), .Q(d_ff_1_q), .reset(Reset_out));  // open: Qn, preset, en
  Button Reset (.out(Reset_out));
  S_MIPS s_mips_1 (
    .Kbd_Enable(KDB[0]), .Address(Addr), .Kbd_Clear(KDB[1]), .Kbd_Available(KDB[2]), .RAM_In_0(I0),
    .Kbd_ASCII_Data(KDB_DATA), .RAM_In_1(I1), .TTY_Enable(TTY_EN), .RAM_In_2(I2), .RAM_In_3(I3),
    .TTY_ASCII_Data(TTY_DATA), .Reset(RST), .RAM_Out_0(ram_1_data_out_0), .Clock(CLK),
    .RAM_Out_1(ram_1_data_out_1), .Stop(halt), .RAM_Out_2(ram_1_data_out_2), .RAM_Out_3(ram_1_data_out_3),
    .Mask(Mask), .Read_Time(ram_1_read_time), .Write_Time(ram_1_write_time), .nRead_Write(R_W),
    .Chip_Select(CS));
  D_Flip_Flop d_ff_2 (.clk(CLK), .D(d_ff_1_q), .Qn(LCLR), .reset(Reset_out));  // open: Q, preset, en
  or or_1 (RST, LCLR, LoadRAM);
  Clock clock_1 (.out(CLK));
  Multiplexer #(.width(32), .enable("false")) multiplexer_1 (.in0(I0), .in1(LData), .out(RI0), .sel(LoadRAM));
  Multiplexer #(.width(32), .enable("false")) multiplexer_2 (.in0(I1), .in1(LData), .out(RI1), .sel(LoadRAM));
  Multiplexer #(.width(32), .enable("false")) multiplexer_3 (.in0(I2), .in1(LData), .out(RI2), .sel(LoadRAM));
  Multiplexer #(.width(32), .enable("false")) multiplexer_4 (.in0(I3), .in1(LData), .out(RI3), .sel(LoadRAM));
  and and_1 (LoadRAM, ~DESHABILITAR_DISPATCHER, LoadRAMOn);  // AND_Gate
  Multiplexer #(.width(16), .enable("false")) multiplexer_5 (.in0(Addr), .in1(LAddr), .out(RAddr), .sel(LoadRAM));
  Multiplexer #(.width(4), .enable("false")) multiplexer_6 (.in0(Mask), .in1(LMask), .out(RMask), .sel(LoadRAM));
  Multiplexer #(.enable("false")) multiplexer_7 (.in0(CS), .in1(LW), .out(RCS), .sel(LoadRAM));
  Multiplexer #(.enable("false")) multiplexer_8 (.in0(R_W), .in1(LW), .out(R_R_W), .sel(LoadRAM));

  // Notes on the sheet:
  //   NO MODIFICAR
  //   Keyboard
endmodule

module RAM (
  input  [15:0] Address,
  input  [31:0] Data_In_0,
  input  [31:0] Data_In_1,
  input  [31:0] Data_In_2,
  input  [31:0] Data_In_3,
  input  [3:0] Mask,
  input  nRead_Write,
  input  Chip_Select,
  input  Reset,
  output [31:0] Data_Out_0,
  output [31:0] Data_Out_1,
  output [31:0] Data_Out_2,
  output [31:0] Data_Out_3,
  output [3:0] Read_Time,
  output [3:0] Write_Time
);

  wire and_2_out, and_3_out, and_4_out, and_5_out, and_6_out, and_7_out, and_8_out, and_9_out, Changed, CLK,
       comparator_2_eq, comparator_3_eq, comparator_4_eq, comparator_5_eq, comparator_6_eq, Count,
       demultiplexer_3_out0, Idle, Idle_q, Load, Load0, Load1, nand_1_out, or_1_out, or_2_out, or_3_out,
       or_4_out, or_5_out, or_6_out, or_7_out, or_8_out, or_9_out, or_10_out, Proc_q, Update_Mem, Zero_Time;
  wire [3:0] counter_1_q, multiplexer_1_out, subtractor_1_out;
  wire [31:0] register_1_q, register_2_q, register_3_q, register_4_q, register_5_q;

  // Probe on 4'b0011
  // Probe on 4'b0010
  Multiplexer #(.width(4), .enable("false")) multiplexer_1 (
    .in0(4'b0011), .in1(4'b0010), .out(multiplexer_1_out), .sel(nRead_Write));
  or or_1 (or_1_out, Idle, Update_Mem);
  or or_2 (or_2_out, ~Chip_Select, Reset);  // OR_Gate
  Subtractor #(.width(4)) subtractor_1 (.a(multiplexer_1_out), .b(4'b0010), .out(subtractor_1_out));  // open: bin, bout
  D_Flip_Flop u_Idle (.clk(CLK), .D(or_1_out), .Q(Idle_q), .preset(or_2_out));  // open: Qn, en, reset
  Demultiplexer #(.enable("false")) demultiplexer_1 (.out0(Idle), .out1(Load0), .in(Idle_q), .sel(Changed));
  // Probe on counter_1_q
  Counter #(.width(4), .max('hf)) counter_1 (
    .load(Load), .D(subtractor_1_out), .count(Count), .Q(counter_1_q), .clk(CLK), .clr(or_3_out));  // open: carry
  or or_3 (or_3_out, ~Chip_Select, Reset);  // OR_Gate
  Comparator #(.width(4), .mode("unsigned")) comparator_1 (
    .a(4'b0000), .b(counter_1_q), .eq(Zero_Time));  // open: gt, lt
  or or_4 (or_4_out, Count, Load0, Load1);
  Register #(.width(32)) register_1 (.D(Data_In_0), .en(Chip_Select), .Q(register_1_q), .clk(CLK), .clr(or_5_out));
  or or_5 (or_5_out, ~Chip_Select, Reset);  // OR_Gate
  Register #(.width(32)) register_2 (.D(Data_In_1), .en(Chip_Select), .Q(register_2_q), .clk(CLK), .clr(or_6_out));
  or or_6 (or_6_out, ~Chip_Select, Reset);  // OR_Gate
  Register #(.width(32)) register_3 (.D(Data_In_2), .en(Chip_Select), .Q(register_3_q), .clk(CLK), .clr(or_7_out));
  or or_7 (or_7_out, ~Chip_Select, Reset);  // OR_Gate
  Register #(.width(32)) register_4 (.D(Data_In_3), .en(Chip_Select), .Q(register_4_q), .clk(CLK), .clr(or_8_out));
  or or_8 (or_8_out, ~Chip_Select, Reset);  // OR_Gate
  Register #(.width(32)) register_5 (
    .D({{11{1'b1}}, nRead_Write, Mask, Address}), .en(Chip_Select), .Q(register_5_q), .clk(CLK),
    .clr(or_9_out));
  or or_9 (or_9_out, ~Chip_Select, Reset);  // OR_Gate
  D_Flip_Flop Proc (.clk(CLK), .D(or_4_out), .Q(Proc_q), .reset(or_10_out));  // open: Qn, preset, en
  or or_10 (or_10_out, ~Chip_Select, Reset);  // OR_Gate
  Demultiplexer #(.enable("false")) demultiplexer_2 (
    .out0(Count), .out1(Update_Mem), .in(demultiplexer_3_out0), .sel(Zero_Time));
  Demultiplexer #(.enable("false")) demultiplexer_3 (
    .out0(demultiplexer_3_out0), .out1(Load1), .in(Proc_q), .sel(Changed));
  Clock clock_1 (.out(CLK));
  Comparator #(.width(32)) comparator_2 (.a(register_1_q), .b(Data_In_0), .eq(comparator_2_eq));  // open: gt, lt
  Comparator #(.width(32)) comparator_3 (.a(register_2_q), .b(Data_In_1), .eq(comparator_3_eq));  // open: gt, lt
  Comparator #(.width(32)) comparator_4 (.a(register_3_q), .b(Data_In_2), .eq(comparator_4_eq));  // open: gt, lt
  Comparator #(.width(32)) comparator_5 (.a(register_4_q), .b(Data_In_3), .eq(comparator_5_eq));  // open: gt, lt
  Comparator #(.width(32)) comparator_6 (
    .a(register_5_q), .b({{11{1'b1}}, nRead_Write, Mask, Address}), .eq(comparator_6_eq));  // open: gt, lt
  nand nand_1 (nand_1_out, comparator_6_eq, comparator_2_eq, comparator_3_eq, comparator_4_eq, comparator_5_eq);
  and and_1 (Changed, nand_1_out, Chip_Select);
  or or_11 (Load, Count, Load1, Load0);
  and and_2 (and_2_out, Mask[0], Update_Mem, nRead_Write);
  and and_3 (and_3_out, Mask[1], Update_Mem, nRead_Write);
  and and_4 (and_4_out, Mask[2], Update_Mem, nRead_Write);
  and and_5 (and_5_out, Mask[3], Update_Mem, nRead_Write);
  RAM_part #(.addrWidth(16), .dataWidth(32), .bus("separate")) ram_1 (
    .addr(Address), .din(Data_In_0), .data(Data_Out_0), .str(and_2_out), .sel(Chip_Select), .clk(CLK),
    .ld(and_6_out), .clr(Reset));
  and and_6 (and_6_out, ~nRead_Write, Idle);  // AND_Gate
  RAM_part #(.addrWidth(16), .dataWidth(32), .bus("separate")) ram_2 (
    .addr(Address), .din(Data_In_1), .data(Data_Out_1), .str(and_3_out), .sel(Chip_Select), .clk(CLK),
    .ld(and_7_out), .clr(Reset));
  and and_7 (and_7_out, ~nRead_Write, Idle);  // AND_Gate
  RAM_part #(.addrWidth(16), .dataWidth(32), .bus("separate")) ram_3 (
    .addr(Address), .din(Data_In_2), .data(Data_Out_2), .str(and_4_out), .sel(Chip_Select), .clk(CLK),
    .ld(and_8_out), .clr(Reset));
  and and_8 (and_8_out, ~nRead_Write, Idle);  // AND_Gate
  RAM_part #(.addrWidth(16), .dataWidth(32), .bus("separate")) ram_4 (
    .addr(Address), .din(Data_In_3), .data(Data_Out_3), .str(and_5_out), .sel(Chip_Select), .clk(CLK),
    .ld(and_9_out), .clr(Reset));
  and and_9 (and_9_out, ~nRead_Write, Idle);  // AND_Gate

  assign Read_Time = 4'b0011;
  assign Write_Time = 4'b0010;

  // Other names for the same wires on the sheet: M0 = Mask[0]; M1 = Mask[1]; M2 = Mask[2]; M3 = Mask[3];
  //   RW = nRead_Write; CLR = Reset; CS = Chip_Select; Load2 = Count

  // Notes on the sheet:
  //   NO MODIFICAR
  //   excepto quizás los valores RT y WT
  //   BANK0
  //   BANK1
  //   BANK2
  //   BANK3
endmodule

module S_MIPS (
  input  Kbd_Available,
  input  [6:0] Kbd_ASCII_Data,
  input  [31:0] RAM_Out_0,
  input  [31:0] RAM_Out_1,
  input  Reset,
  input  [31:0] RAM_Out_2,
  input  Clock,
  input  [31:0] RAM_Out_3,
  input  [3:0] Read_Time,
  input  [3:0] Write_Time,
  output Kbd_Enable,
  output [15:0] Address,
  output Kbd_Clear,
  output TTY_Enable,
  output [6:0] TTY_ASCII_Data,
  output Stop,
  output [31:0] RAM_In_0,
  output [31:0] RAM_In_1,
  output [31:0] RAM_In_2,
  output [31:0] RAM_In_3,
  output [3:0] Mask,
  output nRead_Write,
  output Chip_Select
);


  // Other names for the same wires on the sheet: CLK = Clock; CLR = Reset; CS = Chip_Select;
  //   KBD_AVAIL = Kbd_Available; KBD_CLR = Kbd_Clear; KBD_DATA[6:0] = Kbd_ASCII_Data; RAM_A[15:0] = Address;
  //   RAM_INPUT_0[31:0] = RAM_In_0; RAM_INPUT_1[31:0] = RAM_In_1; RAM_INPUT_2[31:0] = RAM_In_2;
  //   RAM_INPUT_3[31:0] = RAM_In_3; RAM_MASK[3:0] = Mask; RAM_OUTPUT_0[31:0] = RAM_Out_0;
  //   RAM_OUTPUT_1[31:0] = RAM_Out_1; RAM_OUTPUT_2[31:0] = RAM_Out_2; RAM_OUTPUT_3[31:0] = RAM_Out_3;
  //   RW = nRead_Write; TTY_DATA[6:0] = TTY_ASCII_Data

  // Notes on the sheet:
  //   RAM ADDRESS
  //   DATA FROM RAM
  //   DATA TO RAM
  //   DATA WRITE MASK
  //   RAM TIMING
  //   RAM CONTROL
  //   KEYBOARD
  //   TTY
  //   SEQUENCING
endmodule

module RAM_Dispatcher (
  input  [3:0] WriteTime,
  input  Clock,
  input  CLR,
  output [31:0] Data,
  output [15:0] Address,
  output [3:0] Mask,
  output Finished,
  output Write
);

  wire demultiplexer_2_out1, demultiplexer_3_out1, End, IDLE_q, IncAddr, Load, or_1_out, or_2_out, While_q,
       WriteEnd;
  wire [3:0] counter_1_q;
  wire [31:0] CurrentAddress_q;

  Counter #(.width(32), .max('hffffffff)) CurrentAddress (
    .count(IncAddr), .Q({CurrentAddress_q[31:18], Address, CurrentAddress_q[1:0]}), .clk(Clock), .clr(CLR));  // open: load, D, carry
  or or_1 (or_1_out, IncAddr, demultiplexer_3_out1, Finished);
  D_Flip_Flop IDLE (.clk(Clock), .D(or_1_out), .Q(IDLE_q), .preset(CLR));  // open: Qn, en, reset
  Demultiplexer #(.enable("false")) demultiplexer_1 (.out0(Load), .out1(Finished), .in(IDLE_q), .sel(End));
  D_Flip_Flop While (.clk(Clock), .D(or_2_out), .Q(While_q), .reset(CLR));  // open: Qn, preset, en
  or or_2 (or_2_out, Write, Load);
  RAM_part #(.addrWidth(18), .dataWidth(32)) ram_1 (
    .addr({Address, CurrentAddress_q[1:0]}), .data(Data), .clk(Clock));  // open: sel, ld, clr
  Demultiplexer #(.enable("false")) demultiplexer_2 (
    .out0(Write), .out1(demultiplexer_2_out1), .in(While_q), .sel(WriteEnd));
  Decoder #(.select(2)) decoder_1 (
    .out0(Mask[0]), .out1(Mask[1]), .out2(Mask[2]), .out3(Mask[3]), .sel(CurrentAddress_q[1:0]));  // open: en
  Demultiplexer #(.enable("false")) demultiplexer_3 (
    .out0(IncAddr), .out1(demultiplexer_3_out1), .in(demultiplexer_2_out1), .sel(End));
  Counter #(.width(4), .max('hf)) counter_1 (
    .load(Load), .D(WriteTime), .count(Write), .Q(counter_1_q), .clk(Clock));  // open: carry, clr
  Comparator #(.width(32)) comparator_1 (.a(Data), .b({32{1'b1}}), .eq(End));  // open: gt, lt
  Comparator #(.width(4)) comparator_2 (.a(4'b0000), .b(counter_1_q), .eq(WriteEnd));  // open: gt, lt

  // Other names for the same wires on the sheet: CLK = Clock; Count = Write; WT[3:0] = WriteTime
endmodule

module Register_File (
  input  [31:0] Hi_in,
  input  [4:0] DA,
  input  [31:0] Lo_in,
  input  [31:0] DI,
  input  Save,
  input  [4:0] SA,
  input  [4:0] SB,
  input  Clk,
  input  Reset,
  input  Mul_Div,
  input  stack_instruction,
  input  pop,
  input  pop_load,
  input  push_load,
  output [31:0] Hi_out,
  output [31:0] A,
  output [31:0] Lo_out,
  output [31:0] B,
  output [31:0] SP
);

  wire and_1_out, and_2_out, and_3_out, and_5_out, and_6_out, Aux, Dir0, Dir1, Dir2, Dir3, Dir4, Dir5, Dir6,
       Dir7, Dir8, Dir9, Dir10, Dir11, Dir12, Dir13, Dir14, Dir15, Dir16, Dir17, Dir18, Dir19, Dir20, Dir21,
       Dir22, Dir24, Dir25, Dir26, Dir27, Dir28, Dir29, Dir30, Dir31, DirI23, or_1_out, or_2_out, SP_in,
       Sp_Save;
  wire [31:0] adder_1_out, multiplexer_3_out, Out1, Out2, Out3, Out4, Out5, Out6, Out7, Out8, Out9, Out10,
       Out11, Out12, Out13, Out14, Out15, Out16, Out17, Out18, Out19, Out20, Out21, Out22, Out23, Out24,
       Out25, Out26, Out27, Out28, Out29, Out30, Out31, Sp_Input;

  or or_1 (or_1_out, Save, Aux);
  Decoder #(.select(5), .disabled(0)) decoder_1 (
    .out0(Dir0), .out1(Dir1), .out2(Dir2), .out3(Dir3), .out4(Dir4), .out5(Dir5), .out6(Dir6), .out7(Dir7),
    .out8(Dir8), .out9(Dir9), .out10(Dir10), .out11(Dir11), .out12(Dir12), .out13(Dir13), .out14(Dir14),
    .out15(Dir15), .out16(Dir16), .out17(Dir17), .out18(Dir18), .out19(Dir19), .out20(Dir20), .out21(Dir21),
    .out22(Dir22), .out23(DirI23), .out24(Dir24), .out25(Dir25), .out26(Dir26), .out27(Dir27), .out28(Dir28),
    .out29(Dir29), .out30(Dir30), .out31(Dir31), .sel(DA), .en(or_1_out));
  Register #(.width(32)) register_1 (.D(DI), .en(Dir4), .Q(Out4), .clk(Clk), .clr(Reset));
  Register #(.width(32)) register_2 (.D(DI), .en(Dir8), .Q(Out8), .clk(Clk), .clr(Reset));
  Register #(.width(32)) register_3 (.D(DI), .en(Dir12), .Q(Out12), .clk(Clk), .clr(Reset));
  Register #(.width(32)) register_4 (.D(DI), .en(Dir16), .Q(Out16), .clk(Clk), .clr(Reset));
  Register #(.width(32)) register_5 (.D(DI), .en(Dir20), .Q(Out20), .clk(Clk), .clr(Reset));
  Register #(.width(32)) register_6 (.D(DI), .en(Dir24), .Q(Out24), .clk(Clk), .clr(Reset));
  Register #(.width(32)) register_7 (.D(DI), .en(Dir28), .Q(Out28), .clk(Clk), .clr(Reset));
  Register #(.width(32)) register_8 (.D(DI), .en(Dir1), .Q(Out1), .clk(Clk), .clr(Reset));
  Register #(.width(32)) register_9 (.D(DI), .en(Dir5), .Q(Out5), .clk(Clk), .clr(Reset));
  Register #(.width(32)) register_10 (.D(DI), .en(Dir9), .Q(Out9), .clk(Clk), .clr(Reset));
  Register #(.width(32)) register_11 (.D(DI), .en(Dir13), .Q(Out13), .clk(Clk), .clr(Reset));
  Register #(.width(32)) register_12 (.D(DI), .en(Dir17), .Q(Out17), .clk(Clk), .clr(Reset));
  Register #(.width(32)) register_13 (.D(DI), .en(Dir21), .Q(Out21), .clk(Clk), .clr(Reset));
  Register #(.width(32)) register_14 (.D(DI), .en(Dir25), .Q(Out25), .clk(Clk), .clr(Reset));
  Register #(.width(32)) register_15 (.D(DI), .en(Dir29), .Q(Out29), .clk(Clk), .clr(Reset));
  Multiplexer #(.select(5), .width(32), .enable("false")) multiplexer_1 (
    .in0({32{1'b0}}), .in1(Out1), .in2(Out2), .in3(Out3), .in4(Out4), .in5(Out5), .in6(Out6), .in7(Out7),
    .in8(Out8), .in9(Out9), .in10(Out10), .in11(Out11), .in12(Out12), .in13(Out13), .in14(Out14),
    .in15(Out15), .in16(Out16), .in17(Out17), .in18(Out18), .in19(Out19), .in20(Out20), .in21(Out21),
    .in22(Out22), .in23(Out23), .in24(Out24), .in25(Out25), .in26(Out26), .in27(Out27), .in28(Out28),
    .in29(Out29), .in30(Out30), .in31(Out31), .out(A), .sel(SA));
  Register #(.width(32)) register_16 (.D(DI), .en(Dir2), .Q(Out2), .clk(Clk), .clr(Reset));
  Register #(.width(32)) register_17 (.D(DI), .en(Dir6), .Q(Out6), .clk(Clk), .clr(Reset));
  Register #(.width(32)) register_18 (.D(DI), .en(Dir10), .Q(Out10), .clk(Clk), .clr(Reset));
  Register #(.width(32)) register_19 (.D(DI), .en(Dir14), .Q(Out14), .clk(Clk), .clr(Reset));
  Register #(.width(32)) register_20 (.D(DI), .en(Dir18), .Q(Out18), .clk(Clk), .clr(Reset));
  Register #(.width(32)) register_21 (.D(DI), .en(Dir22), .Q(Out22), .clk(Clk), .clr(Reset));
  Register #(.width(32)) register_22 (.D(DI), .en(Dir26), .Q(Out26), .clk(Clk), .clr(Reset));
  Register #(.width(32)) register_23 (.D(DI), .en(Dir30), .Q(Out30), .clk(Clk), .clr(Reset));
  Multiplexer #(.select(5), .width(32), .enable("false")) multiplexer_2 (
    .in0({32{1'b0}}), .in1(Out1), .in2(Out2), .in3(Out3), .in4(Out4), .in5(Out5), .in6(Out6), .in7(Out7),
    .in8(Out8), .in9(Out9), .in10(Out10), .in11(Out11), .in12(Out12), .in13(Out13), .in14(Out14),
    .in15(Out15), .in16(Out16), .in17(Out17), .in18(Out18), .in19(Out19), .in20(Out20), .in21(Out21),
    .in22(Out22), .in23(Out23), .in24(Out24), .in25(Out25), .in26(Out26), .in27(Out27), .in28(Out28),
    .in29(Out29), .in30(Out30), .in31(Out31), .out(B), .sel(SB));
  Register #(.width(32)) register_24 (.D(DI), .en(Dir3), .Q(Out3), .clk(Clk), .clr(Reset));
  Register #(.width(32)) register_25 (.D(DI), .en(Dir7), .Q(Out7), .clk(Clk), .clr(Reset));
  Register #(.width(32)) register_26 (.D(DI), .en(Dir11), .Q(Out11), .clk(Clk), .clr(Reset));
  Register #(.width(32)) register_27 (.D(DI), .en(Dir15), .Q(Out15), .clk(Clk), .clr(Reset));
  Register #(.width(32)) register_28 (.D(DI), .en(Dir19), .Q(Out19), .clk(Clk), .clr(Reset));
  Register #(.width(32)) register_29 (.D(DI), .en(DirI23), .Q(Out23), .clk(Clk), .clr(Reset));
  Register #(.width(32)) register_30 (.D(DI), .en(Dir27), .Q(Out27), .clk(Clk), .clr(Reset));
  Register #(.width(32)) register_31 (.D(Sp_Input), .en(Sp_Save), .Q(SP), .clk(Clk), .clr(Reset));
  Register #(.width(32)) register_32 (.D(Hi_in), .en(Mul_Div), .Q(Hi_out), .clk(Clk), .clr(Reset));
  Register #(.width(32)) register_33 (.D(Lo_in), .en(Mul_Div), .Q(Lo_out), .clk(Clk), .clr(Reset));
  Multiplexer #(.width(32), .enable("false")) multiplexer_3 (
    .in0(32'hfffffffc), .in1(32'h4), .out(multiplexer_3_out), .sel(pop));
  and and_1 (and_1_out, push_load, ~pop);  // AND_Gate
  and and_2 (and_2_out, pop, pop_load);
  Adder #(.width(32)) adder_1 (.a(SP), .b(multiplexer_3_out), .out(adder_1_out));  // open: cin, cout
  and and_3 (and_3_out, SP_in, Save);
  or or_2 (or_2_out, and_1_out, and_2_out);
  and and_4 (Aux, or_2_out, stack_instruction);
  Multiplexer #(.width(32), .enable("false")) multiplexer_4 (
    .in0(DI), .in1(adder_1_out), .out(Sp_Input), .sel(and_5_out));
  and and_5 (and_5_out, stack_instruction, ~and_6_out);  // AND_Gate
  and and_6 (and_6_out, Save, SP_in);
  or or_3 (Sp_Save, and_3_out, Aux);

  // Other names for the same wires on the sheet: DataIn[31:0] = DI; OutA[31:0] = A; OutB[31:0] = B; RST = Reset;
  //   S_I = stack_instruction

  // Notes on the sheet:
  //   Data Address
  //   Data In
  //   Save
  //   Selector A
  //   Selector B
  //   Hi-Lo Implementation
  //   Stack Pointer Implementation
  //   Data A
  //   Data B
endmodule

module ALU (
  input  [31:0] A,
  input  [31:0] B,
  input  [3:0] SEL,
  input  MUL_DIV,
  output [31:0] Output,
  output [31:0] hi,
  output zero,
  output sign,
  output [31:0] lo
);

  wire comparator_1_lt, comparator_2_lt;
  wire [1:0] SEL_Mul_DIV;
  wire [3:2] SEL_R;
  wire [31:0] ADD, AND, DIV_S_hi, DIV_S_low, DIV_u_HI, DIV_u_LO, MUL_U_hi, MUL_U_low, MULT_HI, MULT_LO, NOR,
       OR, SLT, SLT_u, SUB, XOR;

  Adder #(.width(32)) adder_1 (.a(A), .b(B), .out(ADD));  // open: cin, cout
  Subtractor #(.width(32)) subtractor_1 (.a(A), .b(B), .out(SUB));  // open: bin, bout
  Multiplier #(.width(32)) multiplier_1 (.a(A), .b(B), .out(MULT_LO), .cout(MULT_HI));  // open: cin
  Divider #(.width(32)) divider_1 (.a(A), .b(B), .out(DIV_u_LO), .rem(DIV_u_HI));  // open: upper
  MUL_u mul_u_1 (.in_1(A), .in_2(B), .low(MUL_U_low), .hi(MUL_U_hi));
  DIV_s div_s_1 (.in_1(A), .in_2(B), .low(DIV_S_low), .hi(DIV_S_hi));
  Multiplexer #(.select(2), .width(32)) multiplexer_1 (
    .in0(MULT_HI), .in1(MUL_U_hi), .in2(DIV_S_hi), .in3(DIV_u_HI), .out(hi), .sel(SEL_Mul_DIV), .en(MUL_DIV));
  Multiplexer #(.select(2), .width(32)) multiplexer_2 (
    .in0(MULT_LO), .in1(MUL_U_low), .in2(DIV_S_low), .in3(DIV_u_LO), .out(lo), .sel(SEL_Mul_DIV), .en(MUL_DIV));
  assign OR = A | B;  // OR_Gate or_1, 32 bits wide
  assign NOR = ~(A | B);  // NOR_Gate nor_1, 32 bits wide
  assign AND = A & B;  // AND_Gate and_1, 32 bits wide
  assign XOR = A ^ B;  // XOR_Gate xor_1, 32 bits wide
  Subtractor #(.width(4)) subtractor_2 (.a(SEL), .b(4'b0010), .out({SEL_R, SEL_Mul_DIV}));  // open: bin, bout
  Comparator #(.width(32)) comparator_1 (.a(A), .b(B), .lt(comparator_1_lt));  // open: gt, eq
  Comparator #(.width(32), .mode("unsigned")) comparator_2 (.a(A), .b(B), .lt(comparator_2_lt));  // open: gt, eq
  Multiplexer #(.width(32), .enable("false")) multiplexer_3 (
    .in0({32{1'b0}}), .in1(32'h1), .out(SLT), .sel(comparator_1_lt));
  Multiplexer #(.width(32), .enable("false")) multiplexer_4 (
    .in0({32{1'b0}}), .in1(32'h1), .out(SLT_u), .sel(comparator_2_lt));
  Comparator #(.width(32)) comparator_3 (.a(Output), .b({32{1'b0}}), .eq(zero), .lt(sign));  // open: gt
  Multiplexer #(.select(4), .width(32), .enable("false")) multiplexer_5 (
    .in0(ADD), .in1(SUB), .in2(MULT_LO), .in3(MUL_U_low), .in4(DIV_S_low), .in5(DIV_u_LO), .in6(SLT),
    .in7(SLT_u), .in8(AND), .in9(OR), .in10(NOR), .in11(XOR), .out(Output), .sel(SEL));  // open: in12, in13, in14, in15

  // Other names for the same wires on the sheet: OUT[31:0] = Output; SEL_R[1:0] = SEL_Mul_DIV
endmodule

module MUL_u (
  input  [31:0] in_1,
  input  [31:0] in_2,
  output [31:0] low,
  output [31:0] hi
);

  wire C_S_low1, C_S_low2, C_S_low3, carry, carry2, S3;
  wire [31:0] A_S2, AL, AR, ARxBR_hi, ARxBR_low, B_S1, bit_extender_1_out, bit_extender_2_out,
       bit_extender_3_out, bit_extender_4_out, BL, BR, hi1, hi2, low1, low2, S_hi1, S_hi2, S_low1, S_low2;

  Shift shift_1 (.in_1(1'b0), .in_2(ARxBR_low), .Output(carry), .Output_2(low1));
  Shift shift_2 (.in_1(1'b0), .in_2(low1), .Output(carry2), .Output_2(low2));
  Shift shift_3 (.in_1(carry), .in_2(ARxBR_hi), .Output_2(hi1));  // open: Output
  Shift shift_4 (.in_1(carry2), .in_2(hi1), .Output_2(hi2));  // open: Output
  Shifter #(.width(32), .shift("lr")) shifter_1 (.in(in_1), .\dist (5'b00001), .out(AR));
  Shifter #(.width(32), .shift("lr")) shifter_2 (.in(in_2), .\dist (5'b00001), .out(BR));
  Multiplier #(.width(32)) multiplier_1 (.a(AR), .b(BR), .out(ARxBR_low), .cout(ARxBR_hi));  // open: cin
  Adder #(.width(32)) adder_1 (.a(A_S2), .b(low2), .out(S_low1), .cout(C_S_low1));  // open: cin
  Adder #(.width(32)) adder_2 (.a(B_S1), .b(S_low1), .out(S_low2), .cout(C_S_low2));  // open: cin
  assign bit_extender_1_out = {{31{1'b0}}, S3};  // Bit_Extender bit_extender_1
  Adder #(.width(32)) adder_3 (.a(bit_extender_1_out), .b(S_low2), .out(low), .cout(C_S_low3));  // open: cin
  Shifter #(.width(32)) shifter_3 (.in(AR), .\dist (5'b00001), .out(AL));
  Shifter #(.width(32)) shifter_4 (.in(BR), .\dist (5'b00001), .out(BL));
  assign bit_extender_2_out = {{31{1'b0}}, C_S_low1};  // Bit_Extender bit_extender_2
  assign bit_extender_3_out = {{31{1'b0}}, C_S_low2};  // Bit_Extender bit_extender_3
  assign bit_extender_4_out = {{31{1'b0}}, C_S_low3};  // Bit_Extender bit_extender_4
  Multiplexer #(.width(32), .enable("false")) multiplexer_1 (.in0(AL), .in1({32{1'b0}}), .out(A_S2), .sel(in_2[0]));
  Multiplexer #(.width(32), .enable("false")) multiplexer_2 (.in0(BL), .in1({32{1'b0}}), .out(B_S1), .sel(in_1[0]));
  Adder #(.width(32)) adder_4 (.a(bit_extender_2_out), .b(hi2), .out(S_hi1));  // open: cin, cout
  Adder #(.width(32)) adder_5 (.a(bit_extender_3_out), .b(S_hi1), .out(S_hi2));  // open: cin, cout
  Adder #(.width(32)) adder_6 (.a(bit_extender_4_out), .b(S_hi2), .out(hi));  // open: cin, cout
  and and_1 (S3, in_1[0], in_2[0]);

  // Other names for the same wires on the sheet: A[31:0] = in_1; S1 = in_1[0]; B[31:0] = in_2; S2 = in_2[0];
  //   S_hi[31:0] = hi; S_low[31:0] = low
endmodule

module Shift (
  input  in_1,
  input  [31:0] in_2,
  output Output,
  output [31:0] Output_2
);


  assign Output = in_2[31];
  assign Output_2 = {in_2[30:0], in_1};
endmodule

module DIV_s (
  input  [31:0] in_1,
  input  [31:0] in_2,
  output [31:0] low,
  output [31:0] hi
);

  wire S3;
  wire [31:0] low_t, negator_1_out, negator_2_out, negator_3_out, Selected_1, Selected_2;

  Multiplexer #(.width(32), .enable("false")) multiplexer_1 (
    .in0(in_1), .in1(negator_1_out), .out(Selected_1), .sel(in_1[31]));
  Negator #(.width(32)) negator_1 (.in(in_1), .out(negator_1_out));
  Multiplexer #(.width(32), .enable("false")) multiplexer_2 (
    .in0(in_2), .in1(negator_2_out), .out(Selected_2), .sel(in_2[31]));
  Negator #(.width(32)) negator_2 (.in(in_2), .out(negator_2_out));
  Multiplexer #(.width(32), .enable("false")) multiplexer_3 (.in0(low_t), .in1(negator_3_out), .out(low), .sel(S3));
  Negator #(.width(32)) negator_3 (.in(low_t), .out(negator_3_out));
  xor xor_1 (S3, in_1[31], in_2[31]);
  Divider #(.width(32)) divider_1 (.a(Selected_1), .b(Selected_2), .out(low_t), .rem(hi));  // open: upper

  // Other names for the same wires on the sheet: A[31:0] = in_1; S1 = in_1[31]; B[31:0] = in_2; S2 = in_2[31];
  //   real_low[31:0] = low
endmodule

module BRANCH_CONTROL (
  input  [31:0] Rs,
  input  [31:0] PC,
  input  [31:0] Constante2,
  input  [27:0] Constante_Destino,
  input  J,
  input  JR,
  input  BEQ,
  input  BNE,
  input  BLEZ,
  input  BGTZ,
  input  BLTZ,
  input  ZERO,
  input  SIGN,
  output [31:0] pc_2
);

  wire or_1_out, s1, s2, s3, s4, s5, s6;
  wire [1:0] sel;
  wire [31:0] PC_4, PC_4_Constante2;

  Adder #(.width(32)) adder_1 (.a(PC), .b(32'h4), .out(PC_4));  // open: cin, cout
  Adder #(.width(32)) adder_2 (.a(PC_4), .b(Constante2), .out(PC_4_Constante2));  // open: cin, cout
  and and_1 (s1, BEQ, ZERO);
  and and_2 (s2, BNE, ~ZERO);  // AND_Gate
  and and_3 (s3, BLEZ, ~SIGN);  // AND_Gate
  and and_4 (s4, BGTZ, SIGN);
  and and_5 (s5, ~ZERO, ~SIGN);  // AND_Gate
  and and_6 (s6, s5, BLTZ);
  Multiplexer #(.select(2), .width(32), .enable("false")) multiplexer_1 (
    .in0(PC_4), .in1(PC_4_Constante2), .in2({PC[31:28], Constante_Destino}), .in3(Rs), .out(pc_2), .sel(sel));
  or or_1 (or_1_out, s1, s2, s3, s4, s6);
  Priority_Encoder #(.select(2)) priority_encoder_1 (
    .in0(1'b1), .in1(or_1_out), .in2(J), .in3(JR), .out(sel));  // open: gs, en_out, en_in

  // Other names for the same wires on the sheet: destino[31:0] = {PC[31:28], Constante_Destino}; pc_t[31:0] = pc_2
endmodule

module INTRUCTION_DECODER (
  input  [31:0] IN,
  output halt,
  output j,
  output pop,
  output nop,
  output jr,
  output push,
  output tty,
  output beq,
  output sw,
  output rnd,
  output bne,
  output lw,
  output kbd,
  output blez,
  output lw_sw,
  output mfhi,
  output bgtz,
  output logik_i,
  output mflo,
  output bltz,
  output mul_div,
  output pop_push,
  output [3:0] ALU_op,
  output rf_zero,
  output [4:0] Rs,
  output load_rd,
  output [4:0] Rt,
  output load_zero,
  output [4:0] Rd,
  output inmediate,
  output [1:0] data_to_RF,
  output [31:0] constante,
  output [31:0] constante3,
  output [27:0] constante_destino,
  output [31:0] constante2
);

  wire add, add_op, addi, \and , and_25_out, and_26_out, and_27_out, and_28_out, and_29_out, and_op, andi,
       div, divu, mul, mulu, \nor , op_aritmetica, op_code__0, op_code__1, op_code__1x0, \or , or_16_out,
       or_op, ori, slt, slt_op, slti, slti_sltiu, sltiu, sltu, sltu_op, sub, \xor , xor_op, xori;

  and and_1 (addi, ~IN[26], ~IN[27], ~IN[28], IN[29], ~IN[30], ~IN[31]);  // AND_Gate
  and and_2 (andi, ~IN[26], ~IN[27], IN[28], IN[29], ~IN[30], ~IN[31]);  // AND_Gate
  and and_3 (slti_sltiu, ~IN[26], IN[27], ~IN[28], IN[29], ~IN[30], ~IN[31]);  // AND_Gate
  and and_4 (beq, ~IN[26], ~IN[27], IN[28], ~IN[29], ~IN[30], ~IN[31]);  // AND_Gate
  and and_5 (bne, IN[26], ~IN[27], IN[28], ~IN[29], ~IN[30], ~IN[31]);  // AND_Gate
  and and_6 (blez, ~IN[26], IN[27], IN[28], ~IN[29], ~IN[30], ~IN[31]);  // AND_Gate
  and and_7 (bgtz, IN[26], IN[27], IN[28], ~IN[29], ~IN[30], ~IN[31]);  // AND_Gate
  and and_8 (bltz, IN[26], ~IN[27], ~IN[28], ~IN[29], ~IN[30], ~IN[31]);  // AND_Gate
  and and_9 (lw, IN[26], IN[27], ~IN[28], ~IN[29], ~IN[30], IN[31]);  // AND_Gate
  and and_10 (sw, IN[26], IN[27], ~IN[28], IN[29], ~IN[30], IN[31]);  // AND_Gate
  and and_11 (op_code__1, IN[26], IN[27], IN[28], IN[29], IN[30], IN[31]);
  and and_12 (op_code__0, ~IN[26], ~IN[27], ~IN[28], ~IN[29], ~IN[30], ~IN[31]);  // AND_Gate
  and and_13 (op_code__1x0, ~IN[26], ~IN[27], ~IN[28], IN[29], IN[30], IN[31]);  // AND_Gate
  and and_14 (j, ~IN[26], IN[27], ~IN[28], ~IN[29], ~IN[30], ~IN[31]);  // AND_Gate
  or or_1 (add_op, add, addi, lw, sw);
  or or_2 (slt_op, slt, slti);
  or or_3 (sltu_op, sltu, sltiu);
  or or_4 (and_op, andi, \and );
  or or_5 (or_op, \or , ori);
  or or_6 (xor_op, \xor , xori);
  or or_7 (mul_div, mul, mulu, divu, div);
  or or_8 (lw_sw, lw, sw);
  or or_9 (logik_i, andi, ori, xori);
  or or_10 (pop_push, pop, push);
  or or_11 (inmediate, addi, slti_sltiu, lw_sw, andi);
  or or_12 (rf_zero, blez, bgtz, bltz);
  and and_15 (add, ~IN[0], ~IN[1], ~IN[2], ~IN[3], ~IN[4], IN[5], op_code__0);  // AND_Gate
  and and_16 (sub, ~IN[0], IN[1], ~IN[2], ~IN[3], ~IN[4], IN[5], op_code__0);  // AND_Gate
  and and_17 (mul, ~IN[0], ~IN[1], ~IN[2], IN[3], IN[4], ~IN[5], op_code__0);  // AND_Gate
  and and_18 (mulu, IN[0], ~IN[1], ~IN[2], IN[3], ~IN[4], IN[5], op_code__0);  // AND_Gate
  and and_19 (div, ~IN[0], IN[1], ~IN[2], IN[3], IN[4], ~IN[5], op_code__0);  // AND_Gate
  and and_20 (divu, IN[0], IN[1], ~IN[2], IN[3], IN[4], ~IN[5], op_code__0);  // AND_Gate
  and and_21 (\and , ~IN[0], ~IN[1], IN[2], ~IN[3], ~IN[4], IN[5], op_code__0);  // AND_Gate
  and and_22 (\or , IN[0], ~IN[1], IN[2], ~IN[3], ~IN[4], IN[5], op_code__0);  // AND_Gate
  and and_23 (sltiu, IN[0], IN[1], ~IN[2], IN[3], ~IN[4], ~IN[5], slti_sltiu);  // AND_Gate
  and and_24 (ori, IN[0], ~IN[1], IN[2], IN[3], ~IN[4], ~IN[5], op_code__0);  // AND_Gate
  and and_25 (and_25_out, IN[3], IN[4], ~IN[5]);  // AND_Gate
  and and_26 (and_26_out, IN[29], ~IN[30], ~IN[31]);  // AND_Gate
  and and_27 (and_27_out, op_code__0, ~nop, ~and_25_out, ~mfhi, ~jr, ~mflo);  // AND_Gate
  and and_28 (and_28_out, op_aritmetica, ~inmediate);  // AND_Gate
  and and_29 (and_29_out, ~inmediate, ~load_rd);  // AND_Gate
  and and_30 (slti, ~sltiu, slti_sltiu);  // AND_Gate
  or or_13 (op_aritmetica, and_26_out, and_27_out);
  or or_14 (load_rd, mfhi, mflo, and_28_out, pop, rnd, kbd);
  or or_15 (load_zero, and_29_out, sw);
  and and_31 (\nor , IN[0], IN[1], IN[2], ~IN[3], ~IN[4], IN[5], op_code__0);  // AND_Gate
  and and_32 (\xor , ~IN[0], ~IN[1], ~IN[2], IN[3], ~IN[4], IN[5], op_code__0);  // AND_Gate
  and and_33 (slt, ~IN[0], IN[1], ~IN[2], IN[3], ~IN[4], IN[5], op_code__0);  // AND_Gate
  and and_34 (sltu, IN[0], IN[1], ~IN[2], IN[3], ~IN[4], IN[5], op_code__0);  // AND_Gate
  and and_35 (mfhi, ~IN[0], ~IN[1], ~IN[2], ~IN[3], IN[4], ~IN[5], op_code__0);  // AND_Gate
  and and_36 (mflo, ~IN[0], IN[1], ~IN[2], ~IN[3], IN[4], ~IN[5], op_code__0);  // AND_Gate
  and and_37 (nop, ~IN[0], ~IN[1], ~IN[2], ~IN[3], ~IN[4], ~IN[5], op_code__0);  // AND_Gate
  and and_38 (jr, ~IN[0], ~IN[1], ~IN[2], IN[3], ~IN[4], ~IN[5], op_code__0);  // AND_Gate
  and and_39 (xori, ~IN[0], IN[1], IN[2], IN[3], ~IN[4], ~IN[5], op_code__0);  // AND_Gate
  or or_16 (or_16_out, pop, lw);
  Priority_Encoder #(.select(2)) priority_encoder_1 (
    .in0(1'b1), .in1(mfhi), .in2(mflo), .in3(or_16_out), .out(data_to_RF));  // open: gs, en_out, en_in
  and and_40 (halt, IN[0], IN[1], IN[2], IN[3], IN[4], IN[5], op_code__1);
  and and_41 (tty, IN[0], ~IN[1], ~IN[2], ~IN[3], ~IN[4], ~IN[5], op_code__1);  // AND_Gate
  and and_42 (rnd, ~IN[0], IN[1], ~IN[2], ~IN[3], ~IN[4], ~IN[5], op_code__1);  // AND_Gate
  and and_43 (kbd, ~IN[0], ~IN[1], IN[2], ~IN[3], ~IN[4], ~IN[5], op_code__1);  // AND_Gate
  and and_44 (pop, ~IN[0], ~IN[1], ~IN[2], ~IN[3], ~IN[4], ~IN[5], op_code__1x0);  // AND_Gate
  and and_45 (push, IN[0], ~IN[1], ~IN[2], ~IN[3], ~IN[4], ~IN[5], op_code__1x0);  // AND_Gate
  Priority_Encoder #(.select(4)) priority_encoder_2 (
    .in0(add_op), .in1(sub), .in2(mul), .in3(mulu), .in4(div), .in5(divu), .in6(slt_op), .in7(sltu_op),
    .in8(and_op), .in9(or_op), .in10(xor_op), .out(ALU_op));  // open: in11, in12, in13, in14, in15, gs, en_out, en_in

  assign constante = {{17{IN[15]}}, IN[14:0]};
  assign constante2[31:2] = {{15{IN[15]}}, IN[14:0]};
  assign constante3[31:2] = {{16{1'b0}}, IN[15:2]};
  assign constante_destino = {IN[25:0], 2'b00};
  assign Rd = IN[15:11];
  assign Rs = IN[25:21];
  assign Rt = IN[20:16];

  // Other names for the same wires on the sheet: ALU_operator[3:0] = ALU_op; constante_offset[15:0] = IN[15:0];
  //   destino[25:0] = IN[25:0]; func_code[5:0] = IN[5:0]; x[4:0] = IN[10:6]; logic_i = logik_i;
  //   op_code[5:0] = IN[31:26]

  // Notes on the sheet:
  //   Tipo I
  //   Tipo R
  //   Tipo J
endmodule

module DATA_PATH (
  input  [31:0] Data,
  input  en,
  input  pop_load,
  input  push_load,
  input  load_1,
  input  exec_1,
  input  exec_2,
  input  clk,
  input  clear_1,
  input  clear,
  input  [6:0] kbd_data,
  input  kbd_available,
  output MemoryControl,
  output [31:0] register,
  output MC_Read_write,
  output halt,
  output [31:0] pc,
  output tty,
  output [6:0] tty_data,
  output kbd_enable
);

  wire ALU_Sign, ALU_Zero, and_1_out, and_2_out, and_3_out, beq, bgtz, blez, Bltz, bne, d_ff_2_q, inmediate,
       j, jr, load_Rd, load_zero, logic_i, lw, lw_sw, mfhi, mflo, mul_div, nop, or_2_out, or_3_out, or_4_out,
       POP, pop_push, pop_t, push, RF_load, RF_zero, rnd_t, Stack_Instruction, sw, tty_t;
  wire [1:0] data_to_RF;
  wire [3:0] ALU_op;
  wire [4:0] DA, multiplexer_1_out, Rd, Rs, Rt, SB;
  wire [27:0] constante_destino;
  wire [31:0] ALU_Hi, ALU_Lo, ALU_Output, B, bit_extender_1_out, branch_control_1_pc_2, constante,
       constante_2, constante_3, DI, HI_OUT_RF, Instruction_q, kbd_data_t, LO_OUT_RF, multiplexer_5_out,
       multiplexer_6_out, multiplexer_8_out, multiplexer_9_out, multiplexer_12_out, PC_t, RND, SP;
  wire [31:7] A;

  Multiplexer #(.width(5), .enable("false")) multiplexer_1 (.in0(Rt), .in1(Rd), .out(multiplexer_1_out), .sel(load_Rd));
  Multiplexer #(.width(5), .enable("false")) multiplexer_2 (.in0(Rt), .in1({5{1'b0}}), .out(SB), .sel(RF_zero));
  Random #(.width(32)) random_1 (.clk(clk), .out(RND));  // open: next, clr
  and and_1 (and_1_out, ~en, ~sw, ~lw);  // AND_Gate
  Multiplexer #(.width(5), .enable("false")) multiplexer_3 (
    .in0(multiplexer_1_out), .in1({5{1'b0}}), .out(DA), .sel(load_zero));
  or or_1 (Stack_Instruction, pop_push, and_1_out);
  assign bit_extender_1_out = {{25{1'b0}}, kbd_data};  // Bit_Extender bit_extender_1
  or or_2 (or_2_out, lw, pop_t);
  and and_2 (and_2_out, load_1, en);
  or or_3 (or_3_out, clear_1, clear);
  Multiplexer #(.width(32), .enable("false")) multiplexer_4 (
    .in0({32{1'b1}}), .in1(bit_extender_1_out), .out(kbd_data_t), .sel(kbd_available));
  or or_4 (or_4_out, exec_1, and_3_out);
  and and_3 (and_3_out, exec_2, or_2_out);
  Register #(.width(32)) Instruction (.D(Data), .en(and_2_out), .Q(Instruction_q), .clk(clk), .clr(or_3_out));
  Multiplexer #(.select(2), .width(32), .enable("false")) multiplexer_5 (
    .in0(ALU_Output), .in1(HI_OUT_RF), .in2(LO_OUT_RF), .in3(Data), .out(multiplexer_5_out), .sel(data_to_RF));
  D_Flip_Flop #(.trigger("high")) d_ff_1 (.clk(clk), .D(or_4_out), .Q(RF_load));  // open: Qn, preset, en, reset
  INTRUCTION_DECODER intruction_decoder_1 (
    .IN(Instruction_q), .halt(halt), .j(j), .pop(pop_t), .nop(nop), .jr(jr), .push(push), .tty(tty_t),
    .beq(beq), .sw(sw), .rnd(rnd_t), .bne(bne), .lw(lw), .kbd(kbd_enable), .blez(blez), .lw_sw(lw_sw),
    .mfhi(mfhi), .bgtz(bgtz), .logik_i(logic_i), .mflo(mflo), .bltz(Bltz), .mul_div(mul_div),
    .pop_push(pop_push), .ALU_op(ALU_op), .rf_zero(RF_zero), .Rs(Rs), .load_rd(load_Rd), .Rt(Rt),
    .load_zero(load_zero), .Rd(Rd), .data_to_RF(data_to_RF), .constante(constante), .constante3(constante_3),
    .constante_destino(constante_destino), .constante2(constante_2), .inmediate(inmediate));
  Multiplexer #(.width(32), .enable("false")) multiplexer_6 (
    .in0(multiplexer_5_out), .in1(RND), .out(multiplexer_6_out), .sel(rnd_t));
  D_Flip_Flop #(.trigger("high")) d_ff_2 (.Q(d_ff_2_q), .preset(pop_t), .reset(load_1));  // open: clk, D, Qn, en
  Multiplexer #(.width(32), .enable("false")) multiplexer_7 (
    .in0(multiplexer_6_out), .in1(kbd_data_t), .out(DI), .sel(kbd_enable));
  or or_5 (POP, pop_t, d_ff_2_q);
  Multiplexer #(.width(32), .enable("false")) multiplexer_8 (
    .in0(PC_t), .in1(SP), .out(multiplexer_8_out), .sel(pop_push));
  Multiplexer #(.width(32), .enable("false")) multiplexer_9 (
    .in0(constante), .in1(constante_3), .out(multiplexer_9_out), .sel(logic_i));
  Multiplexer #(.width(32), .enable("false")) multiplexer_10 (.in0({A, tty_data}), .in1(B), .out(register), .sel(sw));
  Multiplexer #(.width(32), .enable("false")) multiplexer_11 (
    .in0(multiplexer_8_out), .in1(ALU_Output), .out(pc), .sel(lw_sw));
  Multiplexer #(.width(32), .enable("false")) multiplexer_12 (
    .in0(B), .in1(multiplexer_9_out), .out(multiplexer_12_out), .sel(inmediate));
  ALU alu_1 (
    .A({A, tty_data}), .B(multiplexer_12_out), .SEL(ALU_op), .MUL_DIV(mul_div), .Output(ALU_Output),
    .hi(ALU_Hi), .zero(ALU_Zero), .sign(ALU_Sign), .lo(ALU_Lo));
  Register_File register_file_1 (
    .DA(DA), .DI(DI), .Save(RF_load), .SA(Rs), .SB(SB), .Clk(clk), .Reset(clear), .A({A, tty_data}), .B(B),
    .Hi_in(ALU_Hi), .Lo_in(ALU_Lo), .Mul_Div(mul_div), .Hi_out(HI_OUT_RF), .Lo_out(LO_OUT_RF),
    .stack_instruction(Stack_Instruction), .pop(POP), .pop_load(pop_load), .push_load(push_load), .SP(SP));
  BRANCH_CONTROL branch_control_1 (
    .Rs({A, tty_data}), .PC(PC_t), .Constante2(constante_2), .Constante_Destino(constante_destino), .J(j),
    .JR(jr), .BEQ(beq), .BNE(bne), .BLEZ(blez), .BGTZ(bgtz), .BLTZ(Bltz), .ZERO(ALU_Zero), .SIGN(ALU_Sign),
    .pc_2(branch_control_1_pc_2));
  Register #(.width(32)) u_PC (.D(branch_control_1_pc_2), .en(exec_1), .Q(PC_t), .clk(clk), .clr(clear));
  or or_6 (MemoryControl, pop_push, lw_sw);
  or or_7 (MC_Read_write, push, sw);
  and and_4 (tty, exec_1, tty_t);

  // Other names for the same wires on the sheet: A[6:0] = tty_data; kbd = kbd_enable
endmodule

module CONTROL_UNIT (
  input  in_1,
  input  in_2,
  input  in_3,
  input  in_4,
  input  in_5
);


  // Other names for the same wires on the sheet: CLK = in_1; CLR = in_2; HALT = in_5; MC = in_4; MC_END = in_3
endmodule
